# Fritzing sketch NANO-SIM900 (saved by Fritzing 1.0.2b)
breadboards: 1

parts:
  PL2303_USBtoTTL1 = PL2303_USBtoTTL [part_number=001 package=Pack-tve]
  A1 = sim900 generic
  BAT1 = BC9VPC [package=bc9vpc]
  Компонент1 = Arduino Nano (Rev3.0) (ICSP)  # not connected
  Mod1 = Full Size SD Card Module  # not connected

nets:
  N1: PL2303_USBtoTTL1.GND, A1.Pin_23, A1.Pin_78, A1.Pin_79, A1.Pin_85, BAT1.V-
  N2: PL2303_USBtoTTL1.RXD, A1.Pin_1, A1.Pin_35
  N3: PL2303_USBtoTTL1.TXD, A1.Pin_2, A1.Pin_10
  N4: A1.Pin_77, BAT1.V+

custom parts:
  PL2303_USBtoTTL: Программатор для Arduino PL2303_USBtoTTL
  sim900 generic: sim900 generic one instance of the generic (i.e. not one of the Seeed boards) sim900 modules. It matches the specific board this person has but may do for the general generic sim900 modules.
  BC9VPC: 9V board-mount battery cradle
  Full Size SD Card Module: SD Card Module Slot Socket Reader For Arduino ARM MCU
