# Fritzing sketch NANO_SD_SIM900 (saved by Fritzing 1.0.2b)
breadboards: 1

parts:
  Компонент1 = Arduino Nano (Rev3.0) (ICSP)
  MH-SD_Card_Module1 = MH-SD_Card_Module [part_number=002]
  U1 = SUP500F [package=sup500f]
  A1 = sim900 generic
  BAT1 = BC9VPC [package=bc9vpc]  # not connected

nets (from the breadboard view):
  GND: Компонент1.GND, MH-SD_Card_Module1.connector7, U1.GND
  N1: Компонент1.D2, U1.RX-I
  N2: Компонент1.D3, U1.TX-O
  N3: Компонент1.D7, A1.Pin_8, A1.Pin_16
  N4: Компонент1.D8, A1.Pin_17
  N5: Компонент1.D10, MH-SD_Card_Module1.connector4
  N6: Компонент1.D11/MOSI, MH-SD_Card_Module1.connector3
  N7: Компонент1.D12/MISO, MH-SD_Card_Module1.connector1
  5V: Компонент1.5V, MH-SD_Card_Module1.connector5, U1.VCC
  N8: Компонент1.D13/SCK, MH-SD_Card_Module1.connector2

custom parts:
  sim900 generic: sim900 generic one instance of the generic (i.e. not one of the Seeed boards) sim900 modules. It matches the specific board this person has but may do for the general generic sim900 modules.
  BC9VPC: 9V board-mount battery cradle
